# Fritzing sketch schema (saved by Fritzing 0.9.3b)

parts:
  M1 = MAX485 Breakout [package=THT]
  U1 = ESP32-38PinWide [part_number=ESP32-38PinWide]
  Componente1 = Arduino Nano (Rev3.0)
  XLR1 = XLR3_NCFAH2 [package=xlr3_nc3fah2]
  LED1 = smd LED [color="Red (633nm)" package="1206 [SMD]"]  # not connected

nets:
  N1: M1.RE, M1.VCC
  N2: M1.DI, Componente1.D3
  N3: M1.A, XLR1.G
  N4: M1.B, XLR1.3
  N5: U1.GPIO17, Componente1.D0/RX

custom parts:
  MAX485 Breakout: MAX485 RS485 breakout board
  ESP32-38PinWide: Generic 38-Pin ESP32 with wide format (only access to one side of pins on a breadboard) based on Stephen Lilley's HiLetgo ESP-WROOM-32 ESP32 ESP-32S Development Board.
